// Digital circuit ProjetoMicroarquitetural.dig as structural Verilog
module ProjetoMicroarquitetural (
  input  clk
);

  wire brg_1_p2, brg_1_p8, brg_1_p9, brg_1_p10, multiplexer_2_out, PC_p2, ula_1_p1, ula_1_p2, ula_1_p6,
       ula_1_p8, ula_1_p9, ula_1_p10;
  wire [1:0] add_1_p4, PC_p3;
  wire [19:0] brg_1_p5;
  wire [31:0] add_1_p3, add_1_p5, immext_1_s, MDD_d, ula_1_p7;

  // REG PC: pin names not known; wires that end beside it: clk, PC_p2, PC_p3
  // ADD add_1: pin names not known; wires that end beside it: PC_p2, PC_p3, add_1_p3, add_1_p4, add_1_p5[6:0], {add_1_p5[31:27], brg_1_p5[19:18]}
  ROM #(.isProgramMemory("true")) MI (.A(PC_p3), .D(add_1_p5[0]));  // open: sel
  Multiplexer #(.Selector_Bits(2), .Bits(32)) multiplexer_1 (
    .sel(add_1_p4), .in_1(32'h4), .in_2(ula_1_p7), .in_3(immext_1_s), .out(add_1_p3));  // open: in_0
  IMMEXT immext_1 (.E(brg_1_p5), .S(immext_1_s));  // open: TPIMM
  // BRG brg_1: pin names not known; wires that end beside it: brg_1_p5[7:5], brg_1_p2, brg_1_p5[12:8], brg_1_p5[17:13], brg_1_p5[4:0], brg_1_p2, clk, brg_1_p8, brg_1_p9, brg_1_p10
  Multiplexer multiplexer_2 (.sel(ula_1_p1), .in_0(brg_1_p10), .in_1(immext_1_s[0]), .out(multiplexer_2_out));
  // ULA ula_1: pin names not known; wires that end beside it: ula_1_p1, ula_1_p2, brg_1_p9, multiplexer_2_out, ula_1_p2, ula_1_p6, ula_1_p7, ula_1_p8, ula_1_p9, ula_1_p10
  LED led_1 (.in(ula_1_p6));
  Multiplexer multiplexer_3 (.sel(ula_1_p10), .in_0(MDD_d[0]), .in_1(ula_1_p7[0]), .out(brg_1_p8));
  RAMDualPort #(.AddrBits(5), .Bits(32)) MDD (
    .A(ula_1_p7[4:0]), .Din(ula_1_p7), .str(ula_1_p9), .C(clk), .ld(ula_1_p8), .D(MDD_d));
  // Pins of 1 and 5 and 32 bits meet at ula_1_p7
  // Pins of 1 and 32 bits meet at MDD_d
  // Pins of 1 and 32 bits meet at {add_1_p5[31:27], brg_1_p5, add_1_p5[6:0]}
  // Pins of 1 and 32 bits meet at immext_1_s
endmodule
